# Fritzing sketch 6LED_charlieplex (saved by Fritzing 0.8.5b)
breadboards: 1

parts:
  Part1 = Arduino Uno (Rev3)
  LED1 = LED - 5mm [color="Red (633nm)" package="5 mm [THT]"]
  LED2 = LED - 5mm [color="Red (633nm)" package="5 mm [THT]"]
  LED3 = LED - 5mm [color="Red (633nm)" package="5 mm [THT]"]
  LED4 = LED - 5mm [color="Red (633nm)" package="5 mm [THT]"]
  LED5 = LED - 5mm [color="Red (633nm)" package="5 mm [THT]"]
  LED6 = LED - 5mm [color="Red (633nm)" package="5 mm [THT]"]
  R1 = Resistor [tolerance=±5% resistance=220 package=THT]
  R2 = Resistor [tolerance=±5% resistance=220 package=THT]
  R3 = Resistor [tolerance=±5% resistance=220 package=THT]
  R4 = Rotary Potentiometer (Small) [maximum_resistance=100kΩ package=THT]

nets:
  N1: Part1.A0, R4.wiper
  N2: Part1.GND, R4.leg1
  N3: Part1.D3_PWM, R3.Pin_0
  N4: Part1.D4, R2.Pin_0
  N5: Part1.D5_PWM, R1.Pin_0
  N6: Part1.5V, R4.leg2
  N7: LED1.cathode, LED3.anode, LED5.cathode, LED6.anode, R1.Pin_1
  N8: LED1.anode, LED2.cathode, LED3.cathode, LED4.anode, R2.Pin_1
  N9: LED2.anode, LED4.cathode, LED5.anode, LED6.cathode, R3.Pin_1
